# Fritzing sketch Untitled Sketchdfgdfg (saved by Fritzing 0.9.4)

parts:
  Part1 = Arduino Uno (Rev3) - ICSP
  Squix1 = OLED 0.96" 128x64 I2C SSD1306
  ZS-042_RTC1 = ZS-042 RTC Module
  SW1 = ENCODER_RGB_CA [package=encoder_led_3]
  SM2 = 28BYJ-48 Stepper Motor [part_number=28BYJ-48]
  Driver2 = 28BYJ-48 Driver Module [part_number=ULN2003 package=THT]
  Power_plug1 = Power plug

nets:
  N1: Part1.A0, SW1.C
  N2: Part1.A1, SW1.B
  N3: Part1.A2, SW1.A
  N4: Part1.A4/SDA, Squix1.SCA, ZS-042_RTC1.SDA
  N5: Part1.A5/SCL, Squix1.SCL
  N6: Part1.D8, Driver2.IN1
  N7: Part1.D9_PWM, Driver2.IN2
  N8: Part1.D10_PWM/SS, Driver2.IN3
  N9: Part1.D11_PWM/MOSI, Driver2.IN4
  N10: Part1.GND, SW1.-B
  5V: Part1.5V, Squix1.VCC
  VIN: Part1.VIN, SW1.+, Power_plug1.VCC
  GND: ZS-042_RTC1.GND, Power_plug1.GND
  N11: SM2.blue-pin, Driver2.blue-pin
  N12: SM2.pink-pin, Driver2.pink-pin
  N13: SM2.yellow-pin, Driver2.yellow-pin
  N14: SM2.orange-pin, Driver2.orange-pin
  N15: SM2.red-pin, Driver2.red-pin

custom parts:
  28BYJ-48 Stepper Motor: Unipolar Stepper Motor 28BYJ-48 Top coil - pink & orange Bottom coil - blue & yellow Common rail - red Connector pins: blue - pink - yellow - orange - red
  28BYJ-48 Driver Module: Generic male header
